// Logisim project J-K flip flop.circ as structural Verilog: 4 circuits, main circuit main
module main (
  input  UP_DOWN,
  input  CLOCK,
  output Out1,
  output out_4,
  output Out0
);

  wire and_1_out_3, and_2_out_3, and_3_out_3, and_4_out_3, j_k_ff_1_qn, j_k_ff_2_qn, not_1_out_2, or_1_out,
       or_2_out_3;

  J_K_Flip_Flop #(.trigger("falling")) j_k_ff_1 (
    .J(1'b1), .clk(CLOCK), .K(1'b1), .Q(Out0), .Qn(j_k_ff_1_qn));  // open: preset, en, reset
  NOT not_1 (.in_1(UP_DOWN), .out_2(not_1_out_2));
  AND and_1 (.in_2(Out0), .in_1(UP_DOWN), .out_3(and_1_out_3));
  AND and_2 (.in_2(not_1_out_2), .in_1(j_k_ff_1_qn), .out_3(and_2_out_3));
  or or_1 (or_1_out, and_1_out_3, and_2_out_3);
  J_K_Flip_Flop #(.trigger("falling")) j_k_ff_2 (
    .J(or_1_out), .clk(CLOCK), .K(or_1_out), .Q(out_4), .Qn(j_k_ff_2_qn));  // open: preset, en, reset
  AND and_3 (.in_2(out_4), .in_1(and_1_out_3), .out_3(and_3_out_3));
  AND and_4 (.in_2(and_2_out_3), .in_1(j_k_ff_2_qn), .out_3(and_4_out_3));
  OR or_2 (.in_1(and_3_out_3), .in_2(and_4_out_3), .out_3(or_2_out_3));
  J_K_Flip_Flop #(.trigger("falling")) j_k_ff_3 (
    .J(or_2_out_3), .clk(CLOCK), .K(or_2_out_3), .Q(Out1));  // open: Qn, preset, en, reset

  // Notes on the sheet:
  //   1:UP
  //   0:Down
  //   Out2
endmodule

module AND (
  input  in_1,
  input  in_2,
  output out_3
);

  Transistor #(.\type ("n")) transistor_1 (.in(in_2), .out(out_3), .gate(in_1));
  Transistor #(.gate("br")) transistor_2 (.in(1'b0), .out(out_3), .gate(in_1));
endmodule

module NOT (
  input  in_1,
  output out_2
);

  Transistor transistor_1 (.in(1'b1), .out(out_2), .gate(in_1));
  Transistor #(.\type ("n"), .gate("br")) transistor_2 (.in(1'b0), .out(out_2), .gate(in_1));
endmodule

module OR (
  input  in_1,
  input  in_2,
  output out_3
);

  wire transistor_1_out;

  Transistor #(.\type ("n")) transistor_1 (.in(in_2), .out(transistor_1_out), .gate(in_2));
  Transistor transistor_2 (.in(in_2), .out(out_3), .gate(in_1));
  Transistor transistor_3 (.in(in_1), .out(out_3), .gate(in_2));
  Transistor #(.\type ("n"), .gate("br")) transistor_4 (.in(transistor_1_out), .out(out_3), .gate(in_1));
endmodule
